# Fritzing sketch Tea-Rex (saved by Fritzing 1.0.6)
breadboards: 1

parts:
  DFPlayer_Mini = DFRobot DFPlayer Mini [part_number=DFR0299]
  S1 = Round Pushbutton
  OLED_Display = Module display OLED I2C 128x64 SSD1306 [package=THT]
  Nano = Arduino Nano (Rev3.0)
  MG90S = Basic Servo
  SP1 = SPEAKER [package=pcb_mount_speaker]
  R1 = Resistor [tolerance=±5% resistance=1k package="2010 [SMD]"]
  Poti = Rotary Potentiometer (Large) [maximum_resistance=1kΩ knob_status=50% power=0.5W package=THT]
  X1 = USB Connectors [package=usb-a-s-silk-female]

nets:
  VCC: DFPlayer_Mini.VCC, OLED_Display.VCC, Nano.5V, MG90S.vcc, Poti.leg2, X1.VBUS
  N1: DFPlayer_Mini.RX, R1.Pin_1
  N2: DFPlayer_Mini.TX, Nano.D10
  N3: DFPlayer_Mini.SPK_1, SP1.-
  GND: DFPlayer_Mini.GND-1, DFPlayer_Mini.GND-2, S1.leg0, OLED_Display.GND, Nano.GND, MG90S.gnd, Poti.leg1, X1.GND
  N4: DFPlayer_Mini.SPK_2, SP1.+
  N5: S1.leg1, Nano.D2
  N6: OLED_Display.SCL, Nano.A5
  N7: OLED_Display.SDA, Nano.A4
  N8: Nano.D9, MG90S.pulse
  N9: Nano.D11/MOSI, R1.Pin_0
  N10: Nano.A0, Poti.wiper

custom parts:
  Module display OLED I2C 128x64 SSD1306: Ecran OLED I2C SSD163 de 128x64 avec connexion I2C
